// Logisim project lab3-2circuit.circ as structural Verilog: 1 circuit, main circuit main
module main (
  input  in_1,
  output First_Stop_Event,
  output Second_Stop_Event,
  output Third_Stop_Event,
  output Currently_In_Stop_and_go_Traffic
);

  wire and_1_out, and_2_out, and_3_out, and_4_out, and_5_out, clock_1_out, clock_2_out, clock_3_out,
       clock_4_out, clock_5_out, clock_6_out, First_5_min_timer_carry, not_1_out, not_2_out, not_3_out,
       Second_5_min_timer_carry, Third_5_min_timer_carry;

  Clock clock_1 (.out(clock_1_out));
  D_Flip_Flop d_ff_1 (
    .clk(clock_1_out), .D(in_1), .Q(First_Stop_Event), .preset(First_Stop_Event),
    .reset(First_5_min_timer_carry));  // open: Qn, en
  and and_1 (and_1_out, First_Stop_Event, in_1);
  Clock clock_2 (.out(clock_2_out));
  Counter #(.width(16), .max('h12c)) First_5_min_timer (
    .carry(First_5_min_timer_carry), .clk(and_2_out), .clr(not_1_out));  // open: load, D, count, Q
  and and_2 (and_2_out, First_Stop_Event, clock_3_out);
  Clock clock_3 (.out(clock_3_out));
  not not_1 (not_1_out, First_Stop_Event);
  D_Flip_Flop d_ff_2 (
    .clk(clock_2_out), .D(and_1_out), .Q(Second_Stop_Event), .preset(Second_Stop_Event),
    .reset(Second_5_min_timer_carry));  // open: Qn, en
  and and_3 (and_3_out, First_Stop_Event, Second_Stop_Event, in_1);
  Counter #(.width(16), .max('h12c), .ongoal("load")) Second_5_min_timer (
    .carry(Second_5_min_timer_carry), .clk(and_4_out), .clr(not_2_out));  // open: load, D, count, Q
  and and_4 (and_4_out, Second_Stop_Event, clock_4_out);
  not not_2 (not_2_out, Second_Stop_Event);
  Clock clock_4 (.out(clock_4_out));
  Clock clock_5 (.out(clock_5_out));
  D_Flip_Flop d_ff_3 (
    .clk(clock_5_out), .D(and_3_out), .Q(Third_Stop_Event), .preset(Third_Stop_Event),
    .reset(Third_5_min_timer_carry));  // open: Qn, en
  Counter #(.width(16), .max('h12c), .ongoal("load")) Third_5_min_timer (
    .carry(Third_5_min_timer_carry), .clk(and_5_out), .clr(not_3_out));  // open: load, D, count, Q
  and and_5 (and_5_out, Third_Stop_Event, clock_6_out);
  Clock clock_6 (.out(clock_6_out));
  and and_6 (Currently_In_Stop_and_go_Traffic, Third_Stop_Event, Second_Stop_Event, First_Stop_Event);
  not not_3 (not_3_out, Third_Stop_Event);
endmodule
